# Fritzing sketch Untitled Sketch 2 (saved by Fritzing 0.9.3b)
breadboards: 1

parts:
  Servo_Motore = Basic Servo
  Arduino_UNO = Arduino Uno (Rev3)
  R1 = Rotary Potentiometer (Small) [maximum_resistance=100kΩ package=THT]
  LCD1 = LCD screen
  R2 = Resistor [tolerance=±5% resistance=220 package=THT]
  Buzzer = Piezo Speaker
  Lettore_di_Impronte_Digitali = sensor_biometrico

nets:
  GND: Servo_Motore.gnd, Arduino_UNO.GND, LCD1.R/W, LCD1.LED-, Buzzer.pin1, Lettore_di_Impronte_Digitali.GND
  VCC: Servo_Motore.vcc, Arduino_UNO.5V, R1.leg1, LCD1.VDD, R2.Pin_1
  N1: Servo_Motore.pulse, Arduino_UNO.D9_PWM
  N2: Arduino_UNO.D8, Buzzer.pin2
  N3: Arduino_UNO.D11_PWM/MOSI, LCD1.E
  N4: Arduino_UNO.D12/MISO, LCD1.RS
  N5: Arduino_UNO.D0/RX, Lettore_di_Impronte_Digitali.RX
  N6: Arduino_UNO.D1/TX, Lettore_di_Impronte_Digitali.TX
  N7: Arduino_UNO.D2, LCD1.DB7
  N8: Arduino_UNO.D3_PWM, LCD1.DB6
  N9: Arduino_UNO.D4, LCD1.DB5
  N10: Arduino_UNO.D5_PWM, LCD1.DB4
  3V3: Arduino_UNO.3V3, Lettore_di_Impronte_Digitali.VCC
  N11: R1.wiper, LCD1.V0
  N12: R1.leg2, LCD1.VSS
  N13: LCD1.LED+, R2.Pin_0

custom parts:
  sensor_biometrico: Adafruit Optical Fingerprint Sensor
